# Fritzing sketch Mailbox - fritzing (saved by Fritzing 0.9.4)

parts:
  MKRGSM1 = Arduino MKR GSM 1400
  US-100 = US-100 Ultrasonic Rangefinder
  S1 = SWITCH-MOMENTARY-2 [package=reed_switch_plastic]
  R1 = Resistor [tolerance=±5% resistance=220 package=THT]
  ANT1 = Antenna  # not connected
  U1 = LIPO-2000mAh [package=lipo-2000]  # not connected

nets:
  GND: MKRGSM1.GND, US-100.GND, US-100.GND*, R1.Pin_0
  N1: MKRGSM1.A4, US-100.Trig/Tx
  N2: MKRGSM1.A5, US-100.Echo/Rx
  VCC: MKRGSM1.VCC, US-100.VCC, S1.1
  N3: S1.2, R1.Pin_1
